# Fritzing sketch Capteur_Flowter (saved by Fritzing 0.9.3b)
breadboards: 1

parts:
  Heltec_CubeCell_Dev-Board1 = Heltec CubeCell Dev-Board [part_number=HTCC-AB01]
  LED1 = LED - 5mm [color="Red (633nm)" package="5 mm [THT]"]
  R1 = Resistor [tolerance=±5% resistance=220 package="0603 [SMD]"]
  BAT1 = Battery Holders [package=lipo-1100mAh]  # not connected

nets:
  N1: Heltec_CubeCell_Dev-Board1.pin3, R1.Pin_0
  N2: Heltec_CubeCell_Dev-Board1.pin_11, Heltec_CubeCell_Dev-Board1.pin_14, Heltec_CubeCell_Dev-Board1.pin_18, LED1.cathode
  N3: LED1.anode, R1.Pin_1

custom parts:
  Heltec CubeCell Dev-Board: CubeCell is a part of the Heltec LoRa series and incorporates an ASR6501 processor and SX1262 RF transceiver with an integrated CP2102 USB to serial port interface and onboard SHT1.25 battery interface with integrated lithium battery management system supporting direct solar panel connection.
