# Fritzing sketch lancelot (saved by Fritzing 0.9.3b)
breadboards: 1

parts:
  Relay_5V = Keyes Relay [package=THT]
  Mod1 = Heltec CubeCell Dev-Board V2 [part_number=HTCC-AB01]
  U2 = Vibration Motor- ROB-08449 [package=vibe-motor-10mm]
  U1 = LIPO-1000mAh [package=lipo-1000]
  BAT1 = Battery Holders [package=battery-aa]  # not connected

nets:
  N1: Relay_5V.signal, Mod1.pin2
  N2: Relay_5V.power, Mod1.pin_10
  N3: Relay_5V.ground, Mod1.pin_11, Mod1.pin_14, Mod1.pin_18
  N4: Relay_5V.NC, Relay_5V.C, Relay_5V.NO, U2.+, U1.-
  N5: U2.-, U1.+

custom parts:
  Keyes Relay: The Keyes 5V relay module is suitable for SCM development, home appliance control. It uses a 5V~12V TIL control signal which can control DC / AC signal.
  Heltec CubeCell Dev-Board V2: CubeCell is a part of the Heltec LoRa series and incorporates a PSoC 4000 series processor and SX1262 RF transceiver with an integrated CP2102 USB to serial port interface and onboard SHT1.25 battery interface with integrated lithium battery management system, supporting direct solar panel connection. Links: Heltec CubeCell Dev-Board product page Github

// code stored in the sketch: bluetoothLight.ino
char blueToothVal;           //value sent over via bluetooth
char lastValue;              //stores last state of device (on/off)
 
void setup()
{
 Serial.begin(9600); 
 pinMode(13,OUTPUT);
 pinMode(12,INPUT);
}
 
 
void loop()
{
  if(Serial.available())
  {//if there is data being recieved
    blueToothVal=Serial.read(); //read it
  }
  if (blueToothVal=='n')
  {//if value from bluetooth serial is n
    digitalWrite(13,HIGH);            //switch on LED
    if (lastValue!='n')
      Serial.println(F("LED is on")); //print LED is on
    lastValue=blueToothVal;
  }
  else if (blueToothVal=='f')
  {//if value from bluetooth serial is n
    digitalWrite(13,LOW);             //turn off LED
    if (lastValue!='f')
      Serial.println(F("LED is off")); //print LED is on
    lastValue=blueToothVal;
  }
  delay(250);
}
