# Fritzing sketch PillowTech_2 (saved by Fritzing 0.9.3b)
breadboards: 1

parts:
  SENS1 = SoilWatch 10
  RFM95W1 = RFM95W LoRa Module
  Composant1 = Arduino Pro Mini (3.3V)  # not connected
  Q1 = NPN-Transistor [package="SOT-23 [SMD]"]
  Q2 = NPN-Transistor [package="SOT-23 [SMD]"]
  SENS2 = SoilWatch 10

nets:
  VCC: SENS1.VCC, RFM95W1.13_3.3V, SENS2.VCC
  N1: SENS1.GND, Q1.1
  N2: Q1.2, Q2.2
  N3: Q2.1, SENS2.GND

custom parts:
  SoilWatch 10: SoilWatch 10 - Capacitive soil moisture sensor
  RFM95W LoRa Module: RF Transceiver by Hope RF. Well supported Arduino libraries are available. This Low Power Long Range Transceiver Module for the frequencies 868MHz and 915MHz and it is also available in other versions.
